# Fritzing sketch sketch (saved by Fritzing 0.9.3b)

parts:
  U1 = NodeMCU V1.0
  DHT1 = DHT22 Humidity and Temperature Sensor
  VCC1 = Battery
  Part1 = Soil Moisture Sensor

nets:
  N1: U1.D0, U1.RST
  N2: U1.D2, DHT1.DATA
  N3: U1.D6, Part1.VCC
  N4: U1.D7, DHT1.VDD
  GND: U1.GND, DHT1.GND, VCC1.-, Part1.GND
  N5: U1.Vin, VCC1.+
  N6: U1.A0, Part1.SIG

custom parts:
  NodeMCU V1.0: ESP8266 based NodeMCU
